# Fritzing sketch fsr sketch (saved by Fritzing 0.9.2b)
breadboards: 3

parts:
  xbee1 = Adafruit Xbee Adapter v1.1 [part_number=126]
  J1 = T Cobbler Plus  # not connected
  PSU1 = Adjustable Breadboard Power Supply
  xbee2 = Adafruit Xbee Adapter v1.1 [part_number=126]
  Part1 = Pro Trinket 5V
  PSU2 = Adjustable Breadboard Power Supply
  J2 = Basic Force Sensing Resistor (FSR) [package=THT]
  LED1 = LED - 5mm [color="Red (633nm)" package="5 mm [THT]"]
  LED2 = LED - 5mm [color="Red (633nm)" package="5 mm [THT]"]
  LED3 = LED - 5mm [color="Red (633nm)" package="5 mm [THT]"]
  LED4 = LED - 5mm [color="Red (633nm)" package="5 mm [THT]"]
  R1 = Resistor [tolerance=±5% resistance=220 package=THT]
  R2 = Resistor [tolerance=±5% resistance=220 package=THT]
  R3 = Resistor [tolerance=±5% resistance=220 package=THT]
  R4 = Resistor [tolerance=±5% resistance=220 package=THT]
  R5 = Resistor [tolerance=±5% resistance=220 package=THT]

nets:
  N1: xbee1.3v#1, PSU1.Vout+
  N2: xbee1.gnd, PSU1.Vout-
  N3: xbee2.3v#1, Part1.VBAT, PSU2.Vout+, J2.pin_0, R1.Pin_0, R2.Pin_0, R3.Pin_0, R4.Pin_0
  GND: xbee2.gnd, Part1.GND, PSU2.Vout-, R5.Pin_0
  N4: xbee2.rx, Part1.TXD
  N5: xbee2.tx, Part1.RXD
  N6: Part1.A0, J2.pin_1, R5.Pin_1
  N7: Part1.A1, LED1.cathode
  N8: Part1.A2, LED2.cathode
  N9: Part1.A3, LED3.cathode
  N10: Part1.A4, LED4.cathode
  N11: LED1.anode, R1.Pin_1
  N12: LED2.anode, R2.Pin_1
  N13: LED3.anode, R3.Pin_1
  N14: LED4.anode, R4.Pin_1

custom parts:
  Adafruit Xbee Adapter v1.1: Adafruit Xbee Adapter
  T Cobbler Plus: The T-Cobbler Plus is an add on prototyping board from Adafruit specifically designed for the Raspberry Pi B+ that can break out all those tasty power, GPIO, I2C and SPI pins from the 40-pin header onto a solderless breadboard. This set will make "cobbling together" prototypes with the Pi super easy. The T-Cobbler Plus can plug into any solderless breadboard.
  Pro Trinket 5V: The Pro Trinket 5V is like an Arduino Pro Mini with more pins and USB included. Built with the common core Arduino chip, the ATmega328p, it has 18 GPIO, 2 extra analog inputs, 28K of flash, and 2K of RAM. It has onboard USB bootloading support with Optiboot support, so you can either program your Pro Trinket over USB or with a FTDI cable. The Pro Trinket is programmable using the Arduino IDE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

// code stored in the sketch: fsr sketch.ino
int FsrPin = 0;
int ledPin1 = 15;
int ledPin2 = 16;
int ledPin3 = 17;
int ledPin4 = 18;
int LEDbrightness;
int FsrReading;
int incomingByte = 0;
int bytesAvailable = 0;
int i = 0;
int readSuccess = 0;
int writeCount = 0;
void setup() 
{
  Serial.begin(9600);
  pinMode(ledPin1, OUTPUT);
  pinMode(ledPin2, OUTPUT);
  pinMode(ledPin3, OUTPUT);
  pinMode(ledPin4, OUTPUT);
  pinMode(13, OUTPUT);
  digitalWrite(ledPin1, HIGH);
  digitalWrite(ledPin2, HIGH);
  digitalWrite(ledPin3, HIGH);
  digitalWrite(ledPin4, HIGH);
  digitalWrite(13, LOW);
  
}

void loop() 
{
  FsrReading = analogRead(FsrPin);

  //Serial.print("Analog reading = ");
  if (writeCount == 5000)
  {
    Serial.print(FsrReading);
    writeCount = 0;
  }
  else
  {
    writeCount++;
  }
  //delay(1000);

  bytesAvailable = Serial.available();

  if (bytesAvailable)
  {
     for (i=0;i<bytesAvailable; i++)
        {
          
            incomingByte = Serial.read();
            readSuccess = 1;
            //digitalWrite(15, HIGH);
            //delay(200);
            //digitalWrite(15, HIGH);
        }

        bytesAvailable=0;
        
        //digitalWrite(13, HIGH);
        //delay(1000);
        //digitalWrite(13, LOW);
        
    
    if (readSuccess == 1)
    {
      /*digitalWrite(13, HIGH);
      delay(1000);
      digitalWrite(13, LOW);*/
        switch ((int)incomingByte)
        {
          case 1:
            digitalWrite(ledPin1, LOW);
            digitalWrite(ledPin2, HIGH);
            digitalWrite(ledPin3, HIGH);
            digitalWrite(ledPin4, HIGH);
            break;  
          case 2:
            digitalWrite(ledPin1, LOW);
            digitalWrite(ledPin2, LOW);
            digitalWrite(ledPin3, HIGH);
            digitalWrite(ledPin4, HIGH);
            break;   
          case 3:
            digitalWrite(ledPin1, LOW);
            digitalWrite(ledPin2, LOW);
            digitalWrite(ledPin3, LOW);
            digitalWrite(ledPin4, HIGH);
            break;         
          case 4:
            digitalWrite(ledPin1, LOW);
            digitalWrite(ledPin2, LOW);
            digitalWrite(ledPin3, LOW);
            digitalWrite(ledPin4, LOW);                    
            break;                                  

          default:
            digitalWrite(ledPin1, HIGH);
            digitalWrite(ledPin2, HIGH);
            digitalWrite(ledPin3, HIGH);
            digitalWrite(ledPin4, HIGH);
            break;
        }
        readSuccess = 0;
    }
  }

}
