# Fritzing sketch fsr_ros (saved by Fritzing 0.9.2b)
breadboards: 3

parts:
  xbee3 = Adafruit Xbee Adapter v1.1 [part_number=126]
  J3 = T Cobbler Plus  # not connected
  PSU3 = Adjustable Breadboard Power Supply
  xbee4 = Adafruit Xbee Adapter v1.1 [part_number=126]
  Part3 = Pro Trinket 5V
  PSU4 = Adjustable Breadboard Power Supply
  J4 = Basic Force Sensing Resistor (FSR) [package=THT]
  R6 = Resistor [tolerance=±5% resistance=220 package=THT]

nets:
  N1: xbee3.3v#1, PSU3.Vout+
  N2: xbee3.gnd, PSU3.Vout-
  N3: xbee4.3v#1, Part3.VBAT, PSU4.Vout+, J4.pin_0
  GND: xbee4.gnd, Part3.GND, PSU4.Vout-, R6.Pin_0
  N4: xbee4.rx, Part3.TXD
  N5: xbee4.tx, Part3.RXD
  N6: J4.pin_1, R6.Pin_1

custom parts:
  Adafruit Xbee Adapter v1.1: Adafruit Xbee Adapter
  T Cobbler Plus: The T-Cobbler Plus is an add on prototyping board from Adafruit specifically designed for the Raspberry Pi B+ that can break out all those tasty power, GPIO, I2C and SPI pins from the 40-pin header onto a solderless breadboard. This set will make "cobbling together" prototypes with the Pi super easy. The T-Cobbler Plus can plug into any solderless breadboard.
  Pro Trinket 5V: The Pro Trinket 5V is like an Arduino Pro Mini with more pins and USB included. Built with the common core Arduino chip, the ATmega328p, it has 18 GPIO, 2 extra analog inputs, 28K of flash, and 2K of RAM. It has onboard USB bootloading support with Optiboot support, so you can either program your Pro Trinket over USB or with a FTDI cable. The Pro Trinket is programmable using the Arduino IDE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
