# Fritzing sketch serial_communication_buttons (saved by Fritzing 0.9.2b)
breadboards: 3

parts:
  xbee2 = Adafruit Xbee Adapter v1.1 [part_number=126]
  J2 = T Cobbler Plus  # not connected
  PSU2 = Adjustable Breadboard Power Supply
  PSU3 = Adjustable Breadboard Power Supply
  Part2 = Pro Trinket 5V
  xbee3 = Adafruit Xbee Adapter v1.1 [part_number=126]
  S1 = Pushbutton [package="[THT]"]
  S2 = Pushbutton [package="[THT]"]
  S3 = Pushbutton [package="[THT]"]
  S4 = Pushbutton [package="[THT]"]
  S5 = Pushbutton [package="[THT]"]

nets:
  N1: xbee2.3v#1, PSU2.Vout+
  N2: xbee2.gnd, PSU2.Vout-
  N3: PSU3.Vout+, Part2.VBAT, xbee3.3v#1
  GND: PSU3.Vout-, Part2.GND, xbee3.gnd, S1.Pin_3, S1.Pin_4, S2.Pin_3, S2.Pin_4, S3.Pin_3, S3.Pin_4, S4.Pin_3, S4.Pin_4, S5.Pin_3, S5.Pin_4
  N4: Part2.D4, S5.Pin_1, S5.Pin_2
  N5: Part2.TXD, xbee3.rx
  N6: Part2.RXD, xbee3.tx
  N7: Part2.A0, S1.Pin_1, S1.Pin_2
  N8: Part2.A1, S2.Pin_1, S2.Pin_2
  N9: Part2.A2, S3.Pin_1, S3.Pin_2
  N10: Part2.A3, S4.Pin_1, S4.Pin_2

custom parts:
  Adafruit Xbee Adapter v1.1: Adafruit Xbee Adapter
  T Cobbler Plus: The T-Cobbler Plus is an add on prototyping board from Adafruit specifically designed for the Raspberry Pi B+ that can break out all those tasty power, GPIO, I2C and SPI pins from the 40-pin header onto a solderless breadboard. This set will make "cobbling together" prototypes with the Pi super easy. The T-Cobbler Plus can plug into any solderless breadboard.
  Pro Trinket 5V: The Pro Trinket 5V is like an Arduino Pro Mini with more pins and USB included. Built with the common core Arduino chip, the ATmega328p, it has 18 GPIO, 2 extra analog inputs, 28K of flash, and 2K of RAM. It has onboard USB bootloading support with Optiboot support, so you can either program your Pro Trinket over USB or with a FTDI cable. The Pro Trinket is programmable using the Arduino IDE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
